# Fritzing sketch octopus (saved by Fritzing 0.9.2b)
circuit board: 8.46667cm x 5.64444cm
breadboards: 1

parts:
  元件1 = Arduino Nano (Rev3.0)
  J3 = shrouded pin header, 8 pins [form="♂ (shrouded male)"]

nets:
  N1: 元件1.D7, J3.pin2
  N2: 元件1.D8, J3.pin7
  N3: 元件1.D11/MOSI, J3.pin6
  N4: 元件1.D12/MISO, J3.pin4
  N5: 元件1.GND, J3.pin1
  N6: 元件1.3V3, J3.pin8
  N7: 元件1.D13/SCK, J3.pin3
